// Logisim project rv5i_starter.circ as structural Verilog: 11 circuits, main circuit main
module main (
  input  reset
);

  wire alu0, alug, alul, \bit , branch_control_1_b_out, clk, control_unit_1_alu_src, control_unit_1_branch,
       control_unit_1_jump, control_unit_1_mem_read, control_unit_1_mem_write, halt, iit, jalr, jit,
       regwrite, rit, run_clk, sit, uit, xit;
  wire [1:0] control_unit_1_mem_to_reg;
  wire [2:0] f3;
  wire [3:0] control_unit_1_alu_op;
  wire [4:0] rdi, rs1, rs2;
  wire [6:0] f7;
  wire [9:0] adder_2_out, register_1_q;
  wire [31:0] adder_3_out, alu_out, data_memory_1_read_data, imm, instr, multiplexer_1_out,
       multiplexer_3_out, multiplexer_4_out, multiplexer_5_out, multiplexer_6_out, multiplexer_7_out, pc,
       ppp4, rd, register_file_1_rs1, register_file_1_rs2, shifter_1_out;

  Clock u_clk (.out(clk));
  Multiplexer #(.width(32)) multiplexer_1 (.in0(multiplexer_6_out), .in1(alu_out), .out(multiplexer_1_out), .sel(jalr));
  // Probe on multiplexer_6_out
  Register #(.width(10)) register_1 (.D(adder_2_out), .en(1'b1), .clk(run_clk), .Q(register_1_q), .clr(reset));
  Multiplexer multiplexer_2 (.in0(clk), .in1(1'b0), .out(run_clk), .sel(halt));
  program_counter program_counter_1 (.clk(run_clk), .pc_in(multiplexer_1_out), .reset(reset), .pc(pc));
  instruction_memory instruction_memory_1 (.address(pc), .instruction(instr), .halt(halt));  // open: rdi, rsi1, rsi2
  instruction_decoder instruction_decoder_1 (
    .instr(instr), .rd(rdi), .funct3(f3), .rs1(rs1), .rs2(rs2), .funct7(f7), .imm(imm), .r(rit), .s(sit),
    .u(uit), .nop(xit), .i(iit), .b(\bit ), .j(jit));
  Multiplexer #(.width(32)) multiplexer_3 (.in0(multiplexer_7_out), .in1(ppp4), .out(multiplexer_3_out), .sel(jit));
  // Probe on instr
  // Probe on pc
  // Probe on imm
  // Probe on f3
  // Probe on rs1
  Adder #(.width(32)) adder_1 (.a(pc), .b(32'h4), .out(ppp4));  // open: cin, cout
  Shifter #(.width(32)) shifter_1 (.in(imm), .\dist (5'b00001), .out(shifter_1_out));
  Adder #(.width(10)) adder_2 (.a(register_1_q), .b(10'h1), .out(adder_2_out));  // open: cin, cout
  // Probe on f7
  // Probe on rs2
  Adder #(.width(32)) adder_3 (.a(pc), .b(shifter_1_out), .out(adder_3_out));  // open: cin, cout
  RAM #(.addrWidth(10), .clearpin("true"), .dataWidth(32)) ram_1 (
    .addr(register_1_q), .we(1'b1), .oe(1'b1), .clk(run_clk), .din(instr), .clr(reset));  // open: dout
  // Probe on rdi
  control_unit control_unit_1 (
    .r(rit), .i(iit), .s(sit), .b(\bit ), .u(uit), .j(jit), .nop(xit), .instr(instr),
    .branch(control_unit_1_branch), .mem_read(control_unit_1_mem_read), .mem_write(control_unit_1_mem_write),
    .jump(control_unit_1_jump), .jump_link(jalr), .reg_write(regwrite), .alu_src(control_unit_1_alu_src),
    .alu_op(control_unit_1_alu_op), .mem_to_reg(control_unit_1_mem_to_reg));
  register_file register_file_1 (
    .rsi1(rs1), .rsi2(rs2), .rdi(rdi), .we(regwrite), .clk(run_clk), .reset(reset), .rd(multiplexer_3_out),
    .rs1(register_file_1_rs1), .rs2(register_file_1_rs2));
  Multiplexer #(.width(32)) multiplexer_4 (
    .in0(register_file_1_rs2), .in1(imm), .out(multiplexer_4_out), .sel(control_unit_1_alu_src));
  LED R (.in(rit));
  LED I (.in(iit));
  LED S (.in(sit));
  // Probe on rd
  Multiplexer #(.width(32)) multiplexer_5 (
    .in0(ppp4), .in1(adder_3_out), .out(multiplexer_5_out), .sel(branch_control_1_b_out));
  // Probe on control_unit_1_alu_op
  // Probe on control_unit_1_alu_src
  LED B (.in(\bit ));
  LED U (.in(uit));
  LED J (.in(jit));
  alu alu_1 (
    .b(multiplexer_4_out), .op(control_unit_1_alu_op), .a(register_file_1_rs1), .gt(alug), .lt(alul),
    .zero(alu0), .result(alu_out));  // open: c_out, overflow
  LED X (.in(xit));
  LED STOP (.in(halt));
  Multiplexer #(.width(32)) multiplexer_6 (
    .in0(multiplexer_5_out), .in1(adder_3_out), .out(multiplexer_6_out), .sel(control_unit_1_jump));
  // Probe on alu_out
  data_memory data_memory_1 (
    .clear(reset), .address(alu_out), .write_data(register_file_1_rs2), .clk(run_clk),
    .re(control_unit_1_mem_read), .we(control_unit_1_mem_write), .read_data(data_memory_1_read_data));
  RAM #(.addrWidth(5), .clearpin("true"), .dataWidth(32)) ram_2 (
    .addr(rdi), .we(regwrite), .clk(run_clk), .din(rd), .clr(reset));  // open: oe, dout
  branch_control branch_control_1 (
    .eq(alu0), .lt(alul), .gt(alug), .b_in(control_unit_1_branch), .f3(f3), .b_out(branch_control_1_b_out));
  Multiplexer #(.select(2), .width(32)) multiplexer_7 (
    .in0(alu_out), .in1(data_memory_1_read_data), .in2(ppp4), .in3({32{1'b0}}), .out(multiplexer_7_out),
    .sel(control_unit_1_mem_to_reg));
endmodule

module register_file (
  input  [4:0] rsi1,
  input  [4:0] rsi2,
  input  [4:0] rdi,
  input  [31:0] rd,
  input  we,
  input  clk,
  input  reset,
  output [31:0] rs1,
  output [31:0] rs2
);

  wire we0, we1, we2, we3, we4, we5, we6, we7, we8, we9, we10, we11, we12, we13, we14, we15, we16, we17,
       we18, we19, we20, we21, we22, we23, we24, we25, we26, we27, we28, we29, we30, we31, wesp;
  wire [31:0] rdsp, x1, x2, x3, x4, x5, x6, x7, x8, x9, x10, x11, x12, x13, x14, x15, x16, x17, x18, x19,
       x20, x21, x22, x23, x24, x25, x26, x27, x28, x29, x30, x31;

  Demultiplexer #(.select(5)) demultiplexer_1 (
    .out0(we0), .out1(we1), .out2(we2), .out3(we3), .out4(we4), .out5(we5), .out6(we6), .out7(we7),
    .out8(we8), .out9(we9), .out10(we10), .out11(we11), .out12(we12), .out13(we13), .out14(we14),
    .out15(we15), .out16(we16), .out17(we17), .out18(we18), .out19(we19), .out20(we20), .out21(we21),
    .out22(we22), .out23(we23), .out24(we24), .out25(we25), .out26(we26), .out27(we27), .out28(we28),
    .out29(we29), .out30(we30), .out31(we31), .in(we), .sel(rdi));
  Register #(.width(32)) u_x4 (.D(rd), .en(we4), .clk(clk), .Q(x4), .clr(reset));
  Register #(.width(32)) u_x8 (.D(rd), .en(we8), .clk(clk), .Q(x8), .clr(reset));
  Register #(.width(32)) u_x12 (.D(rd), .en(we12), .clk(clk), .Q(x12), .clr(reset));
  Register #(.width(32)) u_x16 (.D(rd), .en(we16), .clk(clk), .Q(x16), .clr(reset));
  Register #(.width(32)) u_x20 (.D(rd), .en(we20), .clk(clk), .Q(x20), .clr(reset));
  Register #(.width(32)) u_x24 (.D(rd), .en(we24), .clk(clk), .Q(x24), .clr(reset));
  Register #(.width(32)) u_x28 (.D(rd), .en(we28), .clk(clk), .Q(x28), .clr(reset));
  Register #(.width(32)) u_x1 (.D(rd), .en(we1), .clk(clk), .Q(x1), .clr(reset));
  Register #(.width(32)) u_x5 (.D(rd), .en(we5), .clk(clk), .Q(x5), .clr(reset));
  Register #(.width(32)) u_x9 (.D(rd), .en(we9), .clk(clk), .Q(x9), .clr(reset));
  Register #(.width(32)) u_x13 (.D(rd), .en(we13), .clk(clk), .Q(x13), .clr(reset));
  Register #(.width(32)) u_x17 (.D(rd), .en(we17), .clk(clk), .Q(x17), .clr(reset));
  Register #(.width(32)) u_x21 (.D(rd), .en(we21), .clk(clk), .Q(x21), .clr(reset));
  Register #(.width(32)) u_x25 (.D(rd), .en(we25), .clk(clk), .Q(x25), .clr(reset));
  Register #(.width(32)) u_x29 (.D(rd), .en(we29), .clk(clk), .Q(x29), .clr(reset));
  Multiplexer #(.width(32)) multiplexer_1 (.in0(rd), .in1(32'h3e8), .out(rdsp), .sel(reset));
  Register #(.width(32)) u_x2 (.D(rdsp), .en(wesp), .clk(clk), .Q(x2));  // open: clr
  Register #(.width(32)) u_x6 (.D(rd), .en(we6), .clk(clk), .Q(x6), .clr(reset));
  Register #(.width(32)) u_x10 (.D(rd), .en(we10), .clk(clk), .Q(x10), .clr(reset));
  Register #(.width(32)) u_x14 (.D(rd), .en(we14), .clk(clk), .Q(x14), .clr(reset));
  Register #(.width(32)) u_x18 (.D(rd), .en(we18), .clk(clk), .Q(x18), .clr(reset));
  Register #(.width(32)) u_x22 (.D(rd), .en(we22), .clk(clk), .Q(x22), .clr(reset));
  Register #(.width(32)) u_x26 (.D(rd), .en(we26), .clk(clk), .Q(x26), .clr(reset));
  Register #(.width(32)) u_x30 (.D(rd), .en(we30), .clk(clk), .Q(x30), .clr(reset));
  Multiplexer multiplexer_2 (.in0(we2), .in1(1'b1), .out(wesp), .sel(reset));
  Register #(.width(32)) u_x3 (.D(rd), .en(we3), .clk(clk), .Q(x3), .clr(reset));
  Register #(.width(32)) u_x7 (.D(rd), .en(we7), .clk(clk), .Q(x7), .clr(reset));
  Register #(.width(32)) u_x11 (.D(rd), .en(we11), .clk(clk), .Q(x11), .clr(reset));
  Register #(.width(32)) u_x15 (.D(rd), .en(we15), .clk(clk), .Q(x15), .clr(reset));
  Register #(.width(32)) u_x19 (.D(rd), .en(we19), .clk(clk), .Q(x19), .clr(reset));
  Register #(.width(32)) u_x23 (.D(rd), .en(we23), .clk(clk), .Q(x23), .clr(reset));
  Register #(.width(32)) u_x27 (.D(rd), .en(we27), .clk(clk), .Q(x27), .clr(reset));
  Register #(.width(32)) u_x31 (.D(rd), .en(we31), .clk(clk), .Q(x31), .clr(reset));
  Multiplexer #(.select(5), .width(32)) multiplexer_3 (
    .in0({32{1'b0}}), .in1(x1), .in2(x2), .in3(x3), .in4(x4), .in5(x5), .in6(x6), .in7(x7), .in8(x8),
    .in9(x9), .in10(x10), .in11(x11), .in12(x12), .in13(x13), .in14(x14), .in15(x15), .in16(x16), .in17(x17),
    .in18(x18), .in19(x19), .in20(x20), .in21(x21), .in22(x22), .in23(x23), .in24(x24), .in25(x25),
    .in26(x26), .in27(x27), .in28(x28), .in29(x29), .in30(x30), .in31(x31), .out(rs1), .sel(rsi1));
  Multiplexer #(.select(5), .width(32)) multiplexer_4 (
    .in0({32{1'b0}}), .in1(x1), .in2(x2), .in3(x3), .in4(x4), .in5(x5), .in6(x6), .in7(x7), .in8(x8),
    .in9(x9), .in10(x10), .in11(x11), .in12(x12), .in13(x13), .in14(x14), .in15(x15), .in16(x16), .in17(x17),
    .in18(x18), .in19(x19), .in20(x20), .in21(x21), .in22(x22), .in23(x23), .in24(x24), .in25(x25),
    .in26(x26), .in27(x27), .in28(x28), .in29(x29), .in30(x30), .in31(x31), .out(rs2), .sel(rsi2));

  // Notes on the sheet:
  //   Register File
  //   Inputs
  //   Outputs
  //   x0
endmodule

module immediate_gen (
  input  [31:0] instr,
  output [31:0] I_imm,
  output [31:0] S_imm,
  output [31:0] B_imm,
  output [31:0] U_imm,
  output [31:0] J_imm,
  output [31:0] Js_imm,
  output [31:0] Bs_imm
);

  // NoConnect on instr[6:0]
  assign {I_imm[31], Bs_imm[31:12]} = {{20{instr[31]}}, instr[31]};  // Bit_Extender bit_extender_1
  // NoConnect on I_imm[31]
  // NoConnect on {I_imm[31], Bs_imm[31:13]}
  // NoConnect on {I_imm[31], Bs_imm[31:24]}
  Shifter #(.shift("ar"), .width(32)) shifter_1 (
    .in({Bs_imm[23:12], instr[19:12], instr[20], instr[30:21], 1'b0}), .\dist (5'b00001), .out(J_imm));
  Shifter #(.shift("ar"), .width(32)) shifter_2 (
    .in({Bs_imm[31:12], instr[7], instr[30:25], instr[11:8], 1'b0}), .\dist (5'b00001), .out(B_imm));

  assign Bs_imm[11:0] = {instr[7], instr[30:25], instr[11:8], 1'b0};
  assign I_imm[30:0] = {Bs_imm[31:12], instr[30:20]};
  assign Js_imm = {Bs_imm[23:12], instr[19:12], instr[20], instr[30:21], 1'b0};
  assign S_imm = {I_imm[31], Bs_imm[31:12], instr[30:25], instr[11:7]};
  assign U_imm = {Bs_imm[12], instr[30:12], {12{1'b0}}};

  // Other names for the same wires on the sheet: b_imm_shifted[31:1] = {Bs_imm[31:12], instr[7], instr[30:25], instr[11:8]};
  //   j_imm_shifted[31:1] = {Bs_imm[23:12], instr[19:12], instr[20], instr[30:21]}

  // Notes on the sheet:
  //   I-imm
  //   S-imm
  //   B-imm
  //   U-imm
  //   J-imm
endmodule

module instruction_memory (
  input  [31:0] address,
  output [31:0] instruction,
  output [4:0] rdi,
  output [4:0] rsi1,
  output [4:0] rsi2,
  output halt
);

  wire comparator_1_eq, comparator_2_eq;
  wire [9:0] bitselector_1_out;
  wire [31:0] r_addr;

  BitSelector #(.group(10), .width(32)) bitselector_1 (.in(r_addr), .out(bitselector_1_out), .sel(2'b00));
  ROM #(.addrWidth(10), .dataWidth(32)) rom_1 (.addr(bitselector_1_out), .data(instruction));
  Shifter #(.shift("lr"), .width(32)) shifter_1 (.in(address), .\dist (5'b00010), .out(r_addr));
  Comparator #(.width(32)) comparator_1 (.a(instruction), .b({32{1'b0}}), .eq(comparator_1_eq));  // open: gt, lt
  Comparator #(.width(32)) comparator_2 (.a(instruction), .b(32'h73), .eq(comparator_2_eq));  // open: gt, lt
  or or_1 (halt, comparator_1_eq, comparator_2_eq);

  assign rdi = instruction[11:7];
  assign rsi1 = instruction[19:15];
  assign rsi2 = instruction[24:20];

  // Other names for the same wires on the sheet: addr[31:0] = address; ins[31:0] = instruction;
  //   rs1[4:0] = instruction[19:15]; rs2[4:0] = instruction[24:20]

  // Notes on the sheet:
  //   Only use 10 bits for address
  //   contents of rom_1 (hex, n*v repeats v):
  //   500513 300593 8000ef 73 a5c463 13 ff810113 a12223 112023 59863 513 810113 8067 fff58593 fe1ff0ef
  //   412283 550533 12083 810113 8067
  //   halt when instruction is all zeros
  //   or if its an ecall 0x73
endmodule

module alu_control (
  input  [2:0] funct3,
  input  [6:0] funct7,
  input  ar_i,
  input  ar,
  input  br,
  input  lui_auipc,
  output op_add,
  output op_sub,
  output op_sll,
  output op_slt,
  output op_sltu,
  output op_xor,
  output op_srl,
  output op_sra,
  output op_or,
  output op_and,
  output op_beq,
  output op_bne,
  output op_blt,
  output op_bge,
  output op_bltu,
  output op_bgeu,
  output op_rs2_imm
);

  wire and_1_out, and_2_out, and_3_out, and_4_out, and_5_out, and_6_out, and_7_out, and_8_out, and_9_out,
       and_10_out, and_11_out, and_12_out, or_1_out, or_2_out;

  and and_1 (and_1_out, funct3[2], funct3[1], funct3[0]);
  or or_1 (or_1_out, ar_i, ar);
  and and_2 (and_2_out, funct3[2], funct3[1], ~funct3[0]);  // AND_Gate
  and and_3 (and_3_out, funct3[2], ~funct3[1], funct3[0]);  // AND_Gate
  and and_4 (and_4_out, funct7[5], and_3_out);
  and and_5 (and_5_out, and_3_out, ~funct7[5]);  // AND_Gate
  and and_6 (and_6_out, funct3[2], ~funct3[1], ~funct3[0]);  // AND_Gate
  and and_7 (and_7_out, ~funct3[2], funct3[1], funct3[0]);  // AND_Gate
  and and_8 (and_8_out, ~funct3[2], funct3[1], ~funct3[0]);  // AND_Gate
  and and_9 (and_9_out, ~funct3[2], ~funct3[1], funct3[0]);  // AND_Gate
  and and_10 (and_10_out, funct7[5], and_11_out);
  and and_11 (and_11_out, ~funct3[2], ~funct3[1], ~funct3[0]);  // AND_Gate
  and and_12 (and_12_out, ~ar_i, and_10_out);  // AND_Gate
  and and_13 (op_sub, or_1_out, and_12_out);
  and and_14 (op_sll, and_9_out, or_1_out);
  and and_15 (op_slt, and_8_out, or_1_out);
  and and_16 (op_sltu, and_7_out, or_1_out);
  and and_17 (op_xor, and_6_out, or_1_out);
  and and_18 (op_srl, and_5_out, or_1_out);
  and and_19 (op_sra, and_4_out, or_1_out);
  and and_20 (op_or, and_2_out, or_1_out);
  and and_21 (op_and, and_1_out, or_1_out);
  and and_22 (op_beq, and_11_out, br);
  and and_23 (op_bne, and_9_out, br);
  and and_24 (op_blt, and_6_out, br);
  and and_25 (op_bge, and_3_out, br);
  and and_26 (op_bltu, and_2_out, br);
  and and_27 (op_bgeu, and_1_out, br);
  or or_2 (or_2_out, ~funct7[5], ar_i);  // OR_Gate
  and and_28 (op_add, and_11_out, or_2_out);

  assign op_rs2_imm = lui_auipc;
endmodule

module data_memory (
  input  re,
  input  we,
  input  [31:0] address,
  input  [31:0] write_data,
  input  clk,
  input  clear,
  output [31:0] read_data
);

  wire [15:0] addr_mem;

  // NoConnect on address[31:16]
  Shifter #(.shift("lr"), .width(16)) shifter_1 (.in(address[15:0]), .\dist (4'b0010), .out(addr_mem));
  RAM #(.addrWidth(16), .asyncread("true"), .clearpin("true"), .dataWidth(32), .\type ("nonvolatile")) ram_1 (
    .addr(addr_mem), .we(we), .oe(re), .clk(clk), .din(write_data), .dout(read_data), .clr(clear));

  // Other names for the same wires on the sheet: addr[31:0] = address
endmodule

module alu (
  input  [31:0] a,
  input  [31:0] b,
  input  [3:0] op,
  output zero,
  output [31:0] result,
  output overflow,
  output c_out,
  output gt,
  output lt
);

  wire a_sb, alu_set, b_sb, gte, lte, not_3_out, sum_sb, xor_1_out, xor_2_out;
  wire [31:0] a_t, alu_and, alu_or, alu_slt, alu_sum, b_t, not_1_out, not_2_out;

  BitSelector #(.width(32)) bitselector_1 (.in(a_t), .out(a_sb), .sel({5{1'b1}}));
  BitSelector #(.width(32)) bitselector_2 (.in(b_t), .out(b_sb), .sel({5{1'b1}}));
  BitSelector #(.width(32)) bitselector_3 (.in(alu_sum), .out(sum_sb), .sel({5{1'b1}}));
  assign not_1_out = ~b;  // NOT_Gate not_1, 32 bits wide
  assign not_2_out = ~a;  // NOT_Gate not_2, 32 bits wide
  Multiplexer #(.width(32)) multiplexer_1 (.in0(b), .in1(not_1_out), .out(b_t), .sel(op[2]));
  Multiplexer #(.width(32)) multiplexer_2 (.in0(a), .in1(not_2_out), .out(a_t), .sel(op[3]));
  assign alu_and = a_t & b_t;  // AND_Gate and_1, 32 bits wide
  assign alu_or = a_t | b_t;  // OR_Gate or_1, 32 bits wide
  Adder #(.width(32)) adder_1 (.a(a_t), .b(b_t), .out(alu_sum), .cin(op[2]), .cout(c_out));
  // Probe on alu_and
  // Probe on alu_or
  // Probe on alu_sum
  // Probe on alu_slt
  xor xor_1 (xor_1_out, a_sb, b_sb);
  not not_3 (not_3_out, xor_1_out);
  xor xor_2 (xor_2_out, b_sb, sum_sb);
  assign alu_slt = {{31{1'b0}}, alu_set};  // Bit_Extender bit_extender_1
  Comparator #(.width(32)) comparator_1 (.a(result), .b({32{1'b0}}), .gt(gt), .eq(zero), .lt(lt));
  or or_2 (gte, zero, gt);
  or or_3 (lte, zero, lt);
  and and_2 (overflow, not_3_out, xor_2_out);
  xor xor_3 (alu_set, overflow, sum_sb);
  // Probe on alu_set
  Multiplexer #(.select(2), .width(32)) multiplexer_3 (
    .in0(alu_and), .in1(alu_or), .in2(alu_sum), .in3(alu_slt), .out(result), .sel(op[1:0]));

  // Other names for the same wires on the sheet: a_in[31:0] = a; alu_op[3:0] = op; alu_sel[1:0] = op[1:0];
  //   b_inv = op[2]; c_in = op[2]; a_inv = op[3]; alu_ovf = overflow; alu_result[31:0] = result; b_in[31:0] = b
endmodule

module instruction_decoder (
  input  [31:0] instr,
  output [4:0] rd,
  output [2:0] funct3,
  output [4:0] rs1,
  output [4:0] rs2,
  output [6:0] funct7,
  output [31:0] imm,
  output r,
  output i,
  output s,
  output b,
  output u,
  output j,
  output nop
);

  wire comparator_2_eq, comparator_3_eq, comparator_7_eq, comparator_8_eq, comparator_9_eq, comparator_10_eq,
       or_1_out, or_4_out;
  wire [31:0] immediate_gen_1_b_imm, immediate_gen_1_i_imm, immediate_gen_1_j_imm, immediate_gen_1_s_imm,
       immediate_gen_1_u_imm, multiplexer_1_out, multiplexer_2_out, multiplexer_3_out;

  immediate_gen immediate_gen_1 (
    .instr(instr), .I_imm(immediate_gen_1_i_imm), .S_imm(immediate_gen_1_s_imm),
    .B_imm(immediate_gen_1_b_imm), .U_imm(immediate_gen_1_u_imm), .J_imm(immediate_gen_1_j_imm));  // open: Bs_imm, Js_imm
  Comparator #(.width(7)) comparator_1 (.a(instr[6:0]), .b(7'b0110011), .eq(r));  // open: gt, lt
  Comparator #(.width(7)) comparator_2 (.a(instr[6:0]), .b(7'b0010011), .eq(comparator_2_eq));  // open: gt, lt
  Comparator #(.width(7)) comparator_3 (.a(instr[6:0]), .b(7'b0000011), .eq(comparator_3_eq));  // open: gt, lt
  Comparator #(.width(7)) comparator_4 (.a(instr[6:0]), .b(7'b0100011), .eq(s));  // open: gt, lt
  Comparator #(.width(7)) comparator_5 (.a(instr[6:0]), .b(7'b1100011), .eq(b));  // open: gt, lt
  Comparator #(.width(7)) comparator_6 (.a(instr[6:0]), .b(7'b1101111), .eq(j));  // open: gt, lt
  Comparator #(.width(7)) comparator_7 (.a(instr[6:0]), .b(7'b1100111), .eq(comparator_7_eq));  // open: gt, lt
  Comparator #(.width(7)) comparator_8 (.a(instr[6:0]), .b(7'b0110111), .eq(comparator_8_eq));  // open: gt, lt
  Comparator #(.width(7)) comparator_9 (.a(instr[6:0]), .b(7'b0010111), .eq(comparator_9_eq));  // open: gt, lt
  Comparator #(.width(7)) comparator_10 (.a(instr[6:0]), .b(7'b1110011), .eq(comparator_10_eq));  // open: gt, lt
  Multiplexer #(.width(32)) multiplexer_1 (
    .in0(immediate_gen_1_i_imm), .in1(immediate_gen_1_s_imm), .out(multiplexer_1_out), .sel(s));
  Multiplexer #(.width(32)) multiplexer_2 (
    .in0(multiplexer_1_out), .in1(immediate_gen_1_b_imm), .out(multiplexer_2_out), .sel(b));
  Multiplexer #(.width(32)) multiplexer_3 (
    .in0(multiplexer_2_out), .in1(immediate_gen_1_u_imm), .out(multiplexer_3_out), .sel(or_1_out));
  or or_1 (or_1_out, comparator_9_eq, comparator_8_eq);
  Multiplexer #(.width(32)) multiplexer_4 (.in0(multiplexer_3_out), .in1(immediate_gen_1_j_imm), .out(imm), .sel(j));
  or or_2 (i, comparator_2_eq, comparator_3_eq, comparator_7_eq, comparator_10_eq);
  or or_3 (u, comparator_8_eq, comparator_9_eq);
  or or_4 (or_4_out, r, i, s, b, u, j);
  not not_1 (nop, or_4_out);

  assign funct3 = instr[14:12];
  assign funct7 = instr[31:25];
  assign rd = instr[11:7];
  assign rs1 = instr[19:15];
  assign rs2 = instr[24:20];

  // Other names for the same wires on the sheet: b_type = b; i_type = i; j_type = j; r_type = r; s_type = s;
  //   u_type = u; x_type = nop
endmodule

module control_unit (
  input  [31:0] instr,
  input  r,
  input  i,
  input  s,
  input  b,
  input  u,
  input  j,
  input  nop,
  output reg_write,
  output alu_src,
  output [3:0] alu_op,
  output branch,
  output mem_read,
  output mem_write,
  output [1:0] mem_to_reg,
  output jump,
  output jump_link
);

  wire alu_add, alu_and, alu_or, alu_slt, alu_sub_r, and_4_out, comparator_8_eq, f3and, f3or, f3slt, f3z,
       f720, or_1_out, or_2_out, or_3_out, or_4_out, or_5_out;

  or or_1 (or_1_out, r, i);
  or or_2 (or_2_out, r, i);
  or or_3 (or_3_out, r, i);
  Comparator #(.width(7)) comparator_1 (.a(instr[31:25]), .b(7'b0100000), .eq(f720));  // open: gt, lt
  Comparator #(.width(3)) comparator_2 (.a(instr[14:12]), .b(3'b000), .eq(f3z));  // open: gt, lt
  and and_1 (alu_or, or_1_out, f3or);
  and and_2 (alu_and, or_2_out, f3and);
  and and_3 (alu_slt, or_3_out, f3slt);
  Comparator #(.width(7)) comparator_3 (.a(instr[6:0]), .b(7'b0000011), .eq(mem_read));  // open: gt, lt
  or or_4 (or_4_out, r, i);
  and and_4 (and_4_out, or_4_out, or_5_out);
  or or_5 (or_5_out, f3z, mem_read);
  Comparator #(.width(3)) comparator_4 (.a(instr[14:12]), .b(3'b110), .eq(f3or));  // open: gt, lt
  and and_5 (alu_sub_r, f720, and_4_out);
  and and_6 (alu_add, and_4_out, ~f720);  // AND_Gate
  // Probe on instr[14:12]
  // Probe on instr[31:25]
  or or_6 (alu_op[2], b, alu_slt, alu_sub_r);
  Comparator #(.width(7)) comparator_5 (.a(instr[6:0]), .b(7'b0100011), .eq(mem_write));  // open: gt, lt
  Comparator #(.width(3)) comparator_6 (.a(instr[14:12]), .b(3'b111), .eq(f3and));  // open: gt, lt
  or or_7 (alu_op[0], alu_slt, alu_or);
  or or_8 (reg_write, r, i, u, j);
  or or_9 (alu_src, i, s);
  or or_10 (alu_op[1], alu_op[2], s, alu_add);
  Comparator #(.width(7)) comparator_7 (.a(instr[6:0]), .b(7'b1100111), .eq(jump_link));  // open: gt, lt
  Comparator #(.width(3)) comparator_8 (.a(instr[14:12]), .b(3'b010), .eq(comparator_8_eq));  // open: gt, lt
  and and_7 (f3slt, comparator_8_eq, ~mem_read);  // AND_Gate

  assign alu_op[3] = 1'b0;
  assign branch = b;
  assign jump = j;
  assign mem_to_reg = {jump_link, mem_read};

  // Other names for the same wires on the sheet: alu_slt_or_bit = alu_op[0]; alu_add_bit = alu_op[1];
  //   alu_sub_bit = alu_op[2]; alu_sub_b = b; b_type = b; f7[6:0] = instr[31:25]; i_type = i;
  //   opcode[6:0] = instr[6:0]; f3[2:0] = instr[14:12]; j_type = j; mem_to_register[1:0] = {jump_link, mem_read};
  //   r_type = r; s_type = s; u_type = u; x_type = nop
endmodule

module program_counter (
  input  [31:0] pc_in,
  input  reset,
  input  clk,
  output [31:0] pc
);

  Register #(.width(32)) pc_reg (.D(pc_in), .en(1'b1), .clk(clk), .Q(pc), .clr(reset));

  // Other names for the same wires on the sheet: pc_val[31:0] = pc
endmodule

module branch_control (
  input  b_in,
  input  [2:0] f3,
  input  eq,
  input  lt,
  input  gt,
  output b_out
);

  wire alu_gte, and_1_out, and_2_out, and_3_out, and_4_out, branch_result, is_beq, is_bge, is_blt, is_bne;

  or or_1 (alu_gte, eq, gt);
  and and_1 (and_1_out, is_blt, lt);
  Multiplexer multiplexer_1 (.in0(1'b0), .in1(branch_result), .out(b_out), .sel(b_in));
  and and_2 (and_2_out, eq, is_beq);
  and and_3 (and_3_out, ~eq, is_bne);  // AND_Gate
  and and_4 (and_4_out, is_bge, alu_gte);
  or or_2 (branch_result, and_2_out, and_3_out, and_1_out, and_4_out);
  and and_5 (is_beq, ~f3[2], ~f3[1], ~f3[0]);  // AND_Gate
  and and_6 (is_bne, ~f3[2], ~f3[1], f3[0]);  // AND_Gate
  and and_7 (is_blt, f3[2], ~f3[1], ~f3[0]);  // AND_Gate
  and and_8 (is_bge, f3[2], ~f3[1], f3[0]);  // AND_Gate

  // Other names for the same wires on the sheet: alu_eq = eq; alu_gt = gt; alu_lt = lt

  // Notes on the sheet:
  //   F3 Codes
  //   MODIFY:  Add support for blt and bge
  //   0x0 = beq
  //   0x1 = bne
  //   0x4 = blt
  //   0x5 = bge
  //   f3=000/beq
  //   f3=001/bne
  //   f3=100/blt
  //   f3=101/bge
  //   MODIFY:  Add support for is_blt & is_bge
endmodule
